# Fritzing sketch hello_gpio_control (saved by Fritzing 1.0.0rc)
breadboards: 1

parts:
  Mod1 = Raspberry Pi 4B
  S1 = Round Pushbutton
  LED1 = LED - 5mm [color="Red (633nm)" current=0.030A package="5 mm [THT]"]
  R1 = Resistor [tolerance=±5% power=0.25W resistance=220 package=THT]

nets:
  N1: Mod1.3V3, S1.leg0
  N2: Mod1.GPIO2, R1.Pin_1
  N3: Mod1.GND, LED1.cathode
  N4: Mod1.GPIO21, S1.leg1
  N5: LED1.anode, R1.Pin_0
